// Logisim project 4bit_ALU-complete.circ as structural Verilog: 6 circuits, main circuit main
module main (
  input  A0,
  input  A1,
  input  A2,
  input  A3,
  input  B0,
  input  B1,
  input  B2,
  input  B3,
  input  S0,
  input  S1,
  output OUT_0,
  output OUT_1,
  output OUT_2,
  output OUT_3
);
endmodule

module _4bit_bitwise_AND (
  input  A0,
  input  A1,
  input  A2,
  input  A3,
  input  B0,
  input  B1,
  input  B2,
  input  B3,
  output F0,
  output out_10,
  output F2,
  output F3
);

  and and_1 (F0, A0, B0);
  and and_2 (out_10, A1, B1);
  and and_3 (F2, A2, B2);
  and and_4 (F3, A3, B3);

  // Notes on the sheet:
  //   F1
endmodule

module _4bit_bitwise_OR (
  input  A0,
  input  A1,
  input  A2,
  input  A3,
  input  B0,
  input  B1,
  input  B2,
  input  B3,
  output F0,
  output out_10,
  output F2,
  output F3
);

  or or_1 (F0, A0, B0);
  or or_2 (out_10, A1, B1);
  or or_3 (F2, A2, B2);
  or or_4 (F3, A3, B3);

  // Notes on the sheet:
  //   F1
endmodule

module _4bit_bitwise_XOR (
  input  A0,
  input  A1,
  input  A2,
  input  A3,
  input  B0,
  input  B1,
  input  B2,
  input  B3,
  output F0,
  output out_10,
  output F2,
  output F3
);

  xor xor_1 (F0, A0, B0);
  xor xor_2 (out_10, A1, B1);
  xor xor_3 (F2, A2, B2);
  xor xor_4 (F3, A3, B3);

  // Notes on the sheet:
  //   F1
endmodule

module _4bit_bitwise_ADD (
  input  A0,
  input  A1,
  input  A2,
  input  A3,
  input  B0,
  input  B1,
  input  B2,
  input  B3,
  output F0,
  output out_10,
  output F2,
  output F3
);

  xor xor_1 (F0, A0, B0);
  xor xor_2 (out_10, A1, B1);
  xor xor_3 (F2, A2, B2);
  xor xor_4 (F3, A3, B3);

  // Notes on the sheet:
  //   F1
endmodule

module _2bit_ripple_carry_adder (
  input  A,
  input  B,
  input  Cin,
  output S,
  output Cout
);

  wire and_1_out, and_2_out, and_3_out;

  xor xor_1 (S, A, B, Cin);
  and and_1 (and_1_out, A, B);
  and and_2 (and_2_out, A, Cin);
  and and_3 (and_3_out, B, Cin);
  ExactlyOne xor_2 (.out(Cout), .in0(and_1_out), .in1(and_2_out), .in2(and_3_out));
endmodule
